# Fritzing sketch Untitled Sketch 2 (saved by Fritzing 1.0.2b)
breadboards: 1

parts:
  Part1 = Arduino Nano (Rev3.0)
  LED1 = LED - 3mm [color="Red (633nm)" current=0.030A package="3 mm [THT]"]
  R1 = Resistor [tolerance=±5% resistance=220 package="0603 [SMD]"]
  R2 = Resistor [tolerance=±5% resistance=220 package="0603 [SMD]"]
  LED2 = LED - 3mm [color="Green (555nm)" current=0.030A package="3 mm [THT]"]

nets:
  N1: Part1.GND, LED1.cathode, LED2.cathode
  N2: Part1.D6, R2.Pin_0
  N3: Part1.D7, R1.Pin_0
  N4: LED1.anode, R1.Pin_1
  N5: R2.Pin_1, LED2.anode
