# Fritzing sketch Untitled Sketch (saved by Fritzing 1.0.2b)
breadboards: 1

parts:
  Part1 = InvenSense MPU6050
  Part2 = Arduino Nano (Rev3.0)

nets:
  VCC: Part1.VCC, Part2.5V
  GND: Part1.GND, Part2.GND
  N1: Part1.SCL, Part2.A5
  N2: Part1.SDA, Part2.A4
