# Fritzing sketch Untitled Sketch 2 (saved by Fritzing 1.0.2b)
breadboards: 2

parts:
  R1 = Resistor [tolerance=±5% power=0.25W resistance=510 package=THT]
  R2 = Resistor [tolerance=±5% power=0.25W resistance=2.0k package=THT]
  Part1 = Arduino Nano (Rev3.0)

nets:
  N1: R1.Pin_0, Part1.GND
  N2: R1.Pin_1, R2.Pin_1, Part1.A6
  N3: R2.Pin_0, Part1.5V
