# Fritzing sketch Untitled Sketch (saved by Fritzing 1.0.2b)
breadboards: 1

parts:
  Mod1 = flyskyr6b
  Part1 = Arduino Nano (Rev3.0)

nets:
  N1: Mod1.CH1, Part1.D3
  VCC: Mod1.VCC, Part1.5V
  N2: Mod1.connector14, Part1.GND

notes:
  Example radio receiver(FS-R6B)
  Normally use(FS-I6B)
  Think this cable like goes to radio controller(FS-I6X)

custom parts:
  flyskyr6b: flysky r6b 6ch rc receiver module. Pcb view is 3*7 header pins, 3 female headers will let the board plug in to the receiver, or connect via wires as you choose.
