# Fritzing sketch Untitled Sketch (saved by Fritzing 1.0.2b)
breadboards: 1

parts:
  M1 = ESC
  Mod2 = flyskyr6b
  Part2 = Arduino Nano (Rev3.0)
  Power_plug1 = Power plug  # not connected
  920KV_Motor1 = DJI 920 KV Motor

nets:
  N1: M1.U, 920KV_Motor1.u
  N2: M1.V, 920KV_Motor1.v
  N3: M1.W, 920KV_Motor1.w
  N4: M1.DATA, Part2.D5
  GND: M1.GND, Mod2.connector14, Mod2.GND, Part2.GND
  5V: M1.5V, Mod2.VCC, Mod2.BAT+, Part2.5V
  N5: Mod2.CH1, Part2.D3

notes:
  Example radio receiver(FS-R6B)
  Normally use(FS-I6B)
  Think this cable like goes to radio controller(FS-I6X)
  Normally Turnigy 2S 1300 mAh
  (2S Lipo Battery)
  Normally HobbyKing 6A ESC with BEC

custom parts:
  flyskyr6b: flysky r6b 6ch rc receiver module. Pcb view is 3*7 header pins, 3 female headers will let the board plug in to the receiver, or connect via wires as you choose.
  DJI 920 KV Motor: DJI Brushless Outrunner 2212/920K Motor F330-550
