# Fritzing sketch Untitled Sketch (saved by Fritzing 1.0.2b)
breadboards: 1

parts:
  D1 = Zener Diode [part_number=1N4732A breakdown_voltage=3.6V package="Melf DO-213 AB [SMD]"]
  R1 = Resistor [tolerance=±5% power=0.25W resistance=510 package=THT]
  D2 = Diode [package=diode-hv]
  R2 = Resistor [tolerance=±5% power=0.25W resistance=510 package=THT]
  M1 = ESC
  R3 = Resistor [tolerance=±5% power=0.25W resistance=2k package=THT]
  Power_plug1 = Power plug
  J1 = XT60 Connector male [package=THT]
  J2 = XT60 Connector female [package=THT]  # not connected
  Part1 = Arduino Nano (Rev3.0)
  U1 = SWITCH_SPDT [package=kps-1290]  # not connected

nets:
  N1: D1.anode, R1.Pin_1, D2.A, Part1.A1
  N2: R2.Pin_0, M1.GND
  N3: R2.Pin_1, R3.Pin_1
  5V: M1.5V, Part1.5V
  GND: Power_plug1.GND, J1.GND
  VCC: Power_plug1.VCC, J1.VCC

notes:
  Think this is BTS50 High-side switch
  zener diode
  power supply

custom parts:
  XT60 Connector male: Yellow XT60 connector for high current loads up to 40A male
  XT60 Connector female: Yellow XT60 connector for high current loads up to 40A female
