# Fritzing sketch Untitled Sketch (saved by Fritzing 1.0.2b)
breadboards: 1

parts:
  R4 = Resistor [tolerance=±5% power=0.25W resistance=2k package=THT]
  R5 = Resistor [tolerance=±5% power=0.25W resistance=510 package=THT]
  M2 = ESC
  Power_plug2 = Power plug
  J3 = XT60 Connector male [package=THT]
  J4 = XT60 Connector female [package=THT]  # not connected
  Part2 = Arduino Nano (Rev3.0)

nets:
  N1: R4.Pin_1, R5.Pin_1
  N2: R5.Pin_0, M2.GND
  5V: M2.5V, Part2.5V
  GND: Power_plug2.GND, J3.GND
  VCC: Power_plug2.VCC, J3.VCC

notes:
  zener diode
  power supply
  Think this is BTS50 High-side switch

custom parts:
  XT60 Connector male: Yellow XT60 connector for high current loads up to 40A male
  XT60 Connector female: Yellow XT60 connector for high current loads up to 40A female
